# Fritzing sketch fritzing_schematic (saved by Fritzing 0.9.3b)
breadboards: 2

parts:
  Part1 = Arduino Nano (Rev3.0)
  Part2 = Arduino Nano (Rev3.0)

nets:
  N1: Part1.A5, Part2.A5
  N2: Part1.A4, Part2.A4
